# Fritzing sketch dimmer (saved by Fritzing 1.0.1rc)
breadboards: 1

parts:
  U1 = 555 Timer [package="DIP8 [THT]"]
  R2 = Resistor [tolerance=±5% power=0.25 resistance=1k package=THT]
  LED1 = LED - 5mm [color="Red (633nm)" current=0.030 package="5 mm [THT]"]
  C1 = Ceramic Capacitor [capacitance=100nF voltage=35V package="100 mil [THT, multilayer]"]
  C2 = Ceramic Capacitor [capacitance=100nF voltage=35V package="100 mil [THT, multilayer]"]
  R3 = Trimmer Potentiometer [maximum_resistance=10kΩ knob_status=50% package=THT]
  R4 = Resistor [tolerance=±5% power=0.25 resistance=220 package=THT]
  AD = mystery part, 3 pins [chip_label=AD]

nets:
  GND: U1.Ground, LED1.cathode, C1.0, C2.0, AD.pin2
  N1: U1.Trigger, U1.Threshold, C1.1, R3.leg1, R3.wiper
  N2: U1.Output, R4.Pin_0, AD.pin3
  5V: U1.Reset, U1.Vcc_Supply_Voltage, R2.Pin_1, AD.pin1
  N3: U1.Control_Voltage, C2.1
  N4: U1.Discharge, R2.Pin_0, R3.leg2
  N5: LED1.anode, R4.Pin_1
